// Logisim project hw4.circ as structural Verilog: 3 circuits, main circuit Processor
module Processor (
  input  reset
);

  wire ALU__WIP_p1, clock_1_out, undriven, undriven_3;
  wire [15:0] adder_1_out, ALU__WIP_p4, and_1_out, bit_extender_1_out, multiplexer_1_out, multiplexer_2_out,
       PC_q, RegisterFile_out1, RegisterFile_out2, rom_1_data, undriven_2;

  Clock clock_1 (.out(clock_1_out));
  Register #(.width(16)) PC (.D(multiplexer_1_out), .Q(PC_q), .clk(clock_1_out), .clr(reset));  // open: en
  Multiplexer #(.width(16)) multiplexer_1 (
    .in0(and_1_out), .in1(adder_1_out), .out(multiplexer_1_out));  // open: sel, en
  Adder #(.width(16)) adder_1 (.a(PC_q), .b(16'h4), .out(adder_1_out));  // open: cin, cout
  ROM #(.addrWidth(16), .dataWidth(16)) rom_1 (.data(rom_1_data));  // open: addr, sel
  assign bit_extender_1_out = {{10{rom_1_data[15]}}, rom_1_data[15:10]};  // Bit_Extender bit_extender_1
  assign and_1_out = undriven_2;  // AND_Gate and_1, 16 bits wide AND_Gate
  RegisterFile RegisterFile (
    .RegWrite(undriven), .Data(ALU__WIP_p4), .reg1__destination(rom_1_data[6:4]), .reg2(rom_1_data[9:7]),
    .clock(clock_1_out), .reset(reset), .out1(RegisterFile_out1), .out2(RegisterFile_out2));  // open: reg3
  Multiplexer #(.width(16)) multiplexer_2 (
    .in0(RegisterFile_out2), .in1(bit_extender_1_out), .out(multiplexer_2_out), .sel(undriven_3));  // open: en
  // ALU ALU__WIP: pin names not known; wires that end beside it: ALU__WIP_p1, RegisterFile_out1, multiplexer_2_out, ALU__WIP_p4
  RAM #(.addrWidth(16), .dataWidth(16)) ram_1 (.clr(reset));  // open: addr, data, sel, clk, ld

  // Notes on the sheet:
  //   CONTROL GOES HERE
endmodule

module RegisterFile (
  input  RegWrite,
  input  [15:0] Data,
  input  [2:0] reg1__destination,
  input  [2:0] reg2,
  input  [2:0] reg3,
  input  clock,
  input  reset,
  output [15:0] out1,
  output [15:0] out2
);

  wire demultiplexer_1_out0, demultiplexer_1_out1, demultiplexer_1_out2, demultiplexer_1_out3,
       demultiplexer_1_out4, demultiplexer_1_out5, demultiplexer_1_out6, demultiplexer_1_out7;
  wire [15:0] Clock_Trigger_q, r0_q, r1_q, r2_q, r3_q, r4_q, r5_q, r6_q, r7_q;

  Register #(.width(16), .trigger("falling")) Clock_Trigger (
    .D(Data), .Q(Clock_Trigger_q), .clk(clock), .clr(reset));  // open: en
  Demultiplexer #(.select(3)) demultiplexer_1 (
    .out0(demultiplexer_1_out0), .out1(demultiplexer_1_out1), .out2(demultiplexer_1_out2),
    .out3(demultiplexer_1_out3), .out4(demultiplexer_1_out4), .out5(demultiplexer_1_out5),
    .out6(demultiplexer_1_out6), .out7(demultiplexer_1_out7), .in(RegWrite), .sel(reg1__destination));  // open: en
  Register #(.width(16), .trigger("high")) r0 (
    .D(Clock_Trigger_q), .Q(r0_q), .clk(demultiplexer_1_out0), .clr(reset));  // open: en
  Register #(.width(16), .trigger("high")) r1 (
    .D(Clock_Trigger_q), .Q(r1_q), .clk(demultiplexer_1_out1), .clr(reset));  // open: en
  Register #(.width(16), .trigger("high")) r2 (
    .D(Clock_Trigger_q), .Q(r2_q), .clk(demultiplexer_1_out2), .clr(reset));  // open: en
  Register #(.width(16), .trigger("high")) r3 (
    .D(Clock_Trigger_q), .Q(r3_q), .clk(demultiplexer_1_out3), .clr(reset));  // open: en
  Register #(.width(16), .trigger("high")) r4 (
    .D(Clock_Trigger_q), .Q(r4_q), .clk(demultiplexer_1_out4), .clr(reset));  // open: en
  Register #(.width(16), .trigger("high")) r5 (
    .D(Clock_Trigger_q), .Q(r5_q), .clk(demultiplexer_1_out5), .clr(reset));  // open: en
  Register #(.width(16), .trigger("high")) r6 (
    .D(Clock_Trigger_q), .Q(r6_q), .clk(demultiplexer_1_out6), .clr(reset));  // open: en
  Register #(.width(16), .trigger("high")) r7 (
    .D(Clock_Trigger_q), .Q(r7_q), .clk(demultiplexer_1_out7), .clr(reset));  // open: en
  Multiplexer #(.select(3), .width(16)) multiplexer_1 (
    .in0(r0_q), .in1(r1_q), .in2(r2_q), .in3(r3_q), .in4(r4_q), .in5(r5_q), .in6(r6_q), .in7(r7_q),
    .out(out1), .sel(reg1__destination));  // open: en
  Multiplexer #(.select(3), .width(16)) multiplexer_2 (
    .in0(r0_q), .in1(r1_q), .in2(r2_q), .in3(r3_q), .in4(r4_q), .in5(r5_q), .in6(r6_q), .in7(r7_q),
    .out(out2), .sel(reg2));  // open: en
endmodule

module ALU (
  input  [15:0] in1___rs,
  input  [15:0] in2___rs_imm,
  output [15:0] dataOut
);

  wire [3:0] bit_extender_1_out, bit_extender_2_out;
  wire [15:0] adder_1_out, not_1_out, shifter_1_out, shifter_2_out, subtractor_1_out, xor_1_out;

  assign xor_1_out = in1___rs ^ in2___rs_imm;  // XOR_Gate xor_1, 16 bits wide
  assign not_1_out = ~in1___rs;  // NOT_Gate not_1, 16 bits wide
  Adder #(.width(16)) adder_1 (.a(in1___rs), .b(in2___rs_imm), .out(adder_1_out));  // open: cin, cout
  Subtractor #(.width(16)) subtractor_1 (.a(in1___rs), .b(in2___rs_imm), .out(subtractor_1_out));  // open: bin, bout
  Bit_Extender #(.in_width(16), .out_width(4)) bit_extender_1 (.in(in2___rs_imm), .out(bit_extender_1_out));
  Bit_Extender #(.in_width(16), .out_width(4)) bit_extender_2 (.in(in2___rs_imm), .out(bit_extender_2_out));
  Shifter #(.width(16), .shift("ar")) shifter_1 (.in(in1___rs), .\dist (bit_extender_1_out), .out(shifter_1_out));
  Shifter #(.width(16)) shifter_2 (.in(in1___rs), .\dist (bit_extender_2_out), .out(shifter_2_out));
  Multiplexer #(.select(4), .width(16)) multiplexer_1 (
    .in0(not_1_out), .in1(xor_1_out), .in2(adder_1_out), .in3(adder_1_out), .in4(subtractor_1_out),
    .in5(shifter_1_out), .in6(shifter_2_out), .out(dataOut));  // open: in7, in8, in9, in10, in11, in12, in13, in14, in15, sel, en
endmodule
